# Fritzing sketch perfboardSchematic (saved by Fritzing 0.9.3b)
perfboards: 1

parts:
  J5V = female pin header, 2 pins [form="♀ (female)"]
  J3_3V = female pin header, 2 pins [form="♀ (female)"]
  Power_plug1 = Power plug
  U1 = Voltage Regulator - 5V [package="TO220 [THT]"]
  Fuse1 = Fuse with Handler [part_number=Htc-15m]
  JLCD = female pin header, 2 pins [form="♀ (female)"]
  JESP_5V = female pin header, 2 pins [form="♀ (female)"]
  U2 = Voltage Regulator - 3.3V [package="TO220 [THT]"]
  J5 = female pin header, 2 pins [form="♀ (female)"]
  JESP_3_3V = female pin header, 2 pins [form="♀ (female)"]
  JI2C = female pin header, 2 pins [form="♀ (female)"]
  Part1 = Arduino Uno (Rev3)
  JBREAKOUTI2C = female pin header, 2 pins [form="♀ (female)"]
  JESP8266 = female pin header, 2 pins [form="♀ (female)"]
  J9 = female pin header, 3 pins [form="♀ (female)"]
  DS1 = DS18B20 1-Wire Temperature Sensor [part_number=DS18B20]
  R1 = Resistor [tolerance=±5% resistance=10k package=THT]
  J10 = female alternating pin header, 3 pins [form="♀ (female)"]
  J11 = female pin header, 2 pins [form="♀ (female)"]
  JLCD_I2C = female pin header, 2 pins [form="♀ (female)"]

nets:
  5V: J5V.pin1, U1.output_voltage, JLCD.pin1, JESP_5V.pin1, Part1.5V, J9.pin1, DS1.VDD, R1.Pin_0, J10.pin1
  GND/SENSORBREAKOUT_GND: J5V.pin2, J3_3V.pin2, Power_plug1.GND, U1.GND, JLCD.pin2, JESP_5V.pin2, U2.GND, J5.pin2, JESP_3_3V.pin2, Part1.GND, J9.pin2, DS1.GND, J10.pin2
  3.3V/SENSORBREAKOUT_3.3: J3_3V.pin1, U2.output_voltage, J5.pin1, JESP_3_3V.pin1, Part1.3V3
  N1: Power_plug1.VCC, Fuse1.Connector1
  12V: U1.input_voltage, Fuse1.Connector2, U2.input_voltage
  SCL: JI2C.pin1, Part1.A5/SCL, JBREAKOUTI2C.pin1, JLCD_I2C.pin1
  SDA: JI2C.pin2, Part1.A4/SDA, JBREAKOUTI2C.pin2, JLCD_I2C.pin2
  ESP_TX: Part1.D10_PWM/SS, JESP8266.pin1, J11.pin1
  ESP_RX: Part1.D11_PWM/MOSI, JESP8266.pin2, J11.pin2
  D2: Part1.D2, J10.pin3
  N2: J9.pin3, DS1.DQ, R1.Pin_1
